# Fritzing sketch lcdRFID (saved by Fritzing 0.9.2b)

parts:
  U1 = LCD-16X2 [package=lcd-16x2_nosilk]
  Part3 = Arduino Pro Mini v13
  Part4 = FTDI Basic Programmer
  R2 = Resistor [tolerance=±5% resistance=68 package=THT]
  R1 = Rotary Potentiometer (Large) [maximum_resistance=100kΩ package=THT]
  Part5 = RFID-RC522-v2

nets:
  GND: U1.VSS, U1.R_W, Part3.GND, Part4.GND, R2.Pin_1, R1.leg2, Part5.GND
  5V: U1.VDD, R1.leg1
  N1: U1.VO, R1.wiper
  LCD_RESET: U1.RS, Part3.D6_PWM
  LCD_ENABLE: U1.E, Part3.D5_PWM
  N2: U1.DB4, Part3.A2
  N3: U1.DB5, Part3.A3
  N4: U1.DB6, Part3.A4
  N5: U1.DB7, Part3.A5
  BACK_LIGHT: U1.A, Part3.D3_PWM
  N6: U1.K, R2.Pin_0
  MCU_RESET: Part3.DTR, Part4.DTR
  N7: Part3.D0/TX, Part4.TXO
  N8: Part3.D1/RX, Part4.RXI
  3.3V: Part3.VCC, Part4.POWER, Part5.3.3V
  SCK: Part3.D13/SCK, Part5.SCK
  N9: Part3.D12/MISO, Part5.MISO
  N10: Part3.D11_PWM/MOSI, Part5.MOSI
  RFID_SELECT: Part3.D10_PWM/SS, Part5.SDA
  RFID_RESET: Part3.D9_PWM, Part5.RST
  RFID_IRQ: Part3.D2, Part5.IRQ

custom parts:
  RFID-RC522-v2: A simple China made RFID-RC522 Reader; do check the pin labels, as this is a MFRC522 based clone.
